// Logisim project project.circ as structural Verilog: 4 circuits, main circuit main
module main (
  input  A,
  input  B,
  input  C,
  input  D,
  input  OFF
);

  wire and_1_out, clock_1_out, not_1_out;
  wire [2:0] counter_1_q;
  wire [4:0] display_function_1_a, display_function_1_b, display_function_1_c,
       multi_bit_shift_register_1_q1__5_bit_output, multi_bit_shift_register_1_q2__5_bit_output,
       multi_bit_shift_register_1_q3__5_bit_output, multi_bit_shift_register_1_q4__5_bit_output,
       multi_bit_shift_register_1_q5__5_bit_output, multiplexer_1_out;

  not not_1 (not_1_out, OFF);
  DotMatrix #(.matrixrows(5)) dotmatrix_1 (
    .col0(multi_bit_shift_register_1_q1__5_bit_output), .col1(multi_bit_shift_register_1_q2__5_bit_output),
    .col2(multi_bit_shift_register_1_q3__5_bit_output), .col3(multi_bit_shift_register_1_q4__5_bit_output),
    .col4(multi_bit_shift_register_1_q5__5_bit_output));
  display_function display_function_1 (
    .x(D), .A(display_function_1_a), .B(display_function_1_b), .C(display_function_1_c), .y(C), .w(A), .z(B));
  Clock clock_1 (.out(clock_1_out));
  and and_1 (and_1_out, not_1_out, clock_1_out);
  Multiplexer #(.select(3), .width(5)) multiplexer_1 (
    .in0(display_function_1_c), .in1(display_function_1_b), .in2(display_function_1_a), .in3({5{1'b0}}),
    .in4({5{1'b0}}), .in5({5{1'b0}}), .in6({5{1'b0}}), .in7({5{1'b0}}), .out(multiplexer_1_out),
    .sel(counter_1_q), .en(not_1_out));
  Counter #(.width(3), .max('h7)) counter_1 (
    .Q(counter_1_q), .clk(and_1_out), .clr(OFF));  // open: load, D, count, carry
  multi_bit_shift_register multi_bit_shift_register_1 (
    .Clock(and_1_out), .Enable(not_1_out), .Clear(OFF), ._5_bit_input(multiplexer_1_out),
    .Q1__5_bit_output(multi_bit_shift_register_1_q1__5_bit_output),
    .Q2__5_bit_output(multi_bit_shift_register_1_q2__5_bit_output),
    .Q3__5_bit_output(multi_bit_shift_register_1_q3__5_bit_output),
    .Q4__5_bit_output(multi_bit_shift_register_1_q4__5_bit_output),
    .Q5__5_bit_output(multi_bit_shift_register_1_q5__5_bit_output));
endmodule

module display_function (
  input  x,
  input  z,
  input  w,
  input  y,
  output [4:0] A,
  output [4:0] B,
  output [4:0] C
);

  wire not_1_out;

  not not_1 (not_1_out, w);
  Multiplexer #(.select(3), .enable("false")) multiplexer_1 (
    .in0(not_1_out), .in1(1'b1), .in2(1'b1), .in3(1'b1), .in4(1'b1), .in5(1'b0), .in6(1'b0), .in7(1'b0),
    .out(A[4]), .sel({x, y, z}));
  Multiplexer #(.select(3), .enable("false")) multiplexer_2 (
    .in0(not_1_out), .in1(1'b0), .in2(1'b1), .in3(not_1_out), .in4(1'b1), .in5(1'b0), .in6(1'b0), .in7(1'b0),
    .out(A[3]), .sel({x, y, z}));
  Multiplexer #(.select(3), .enable("false")) multiplexer_3 (
    .in0(not_1_out), .in1(1'b1), .in2(1'b1), .in3(not_1_out), .in4(1'b1), .in5(1'b0), .in6(1'b0), .in7(1'b0),
    .out(A[2]), .sel({x, y, z}));
  Multiplexer #(.select(3), .enable("false")) multiplexer_4 (
    .in0(not_1_out), .in1(not_1_out), .in2(1'b0), .in3(not_1_out), .in4(not_1_out), .in5(1'b0), .in6(1'b0),
    .in7(1'b0), .out(A[1]), .sel({x, y, z}));
  Multiplexer #(.select(3), .enable("false")) multiplexer_5 (
    .in0(not_1_out), .in1(1'b1), .in2(w), .in3(not_1_out), .in4(1'b1), .in5(1'b0), .in6(1'b0), .in7(1'b0),
    .out(A[0]), .sel({x, y, z}));
  Multiplexer #(.select(3), .enable("false")) multiplexer_6 (
    .in0(not_1_out), .in1(1'b1), .in2(w), .in3(1'b1), .in4(1'b1), .in5(1'b0), .in6(1'b0), .in7(1'b0),
    .out(B[4]), .sel({x, y, z}));
  Multiplexer #(.select(3), .enable("false")) multiplexer_7 (
    .in0(1'b0), .in1(1'b0), .in2(1'b0), .in3(1'b0), .in4(1'b0), .in5(1'b0), .in6(1'b0), .in7(1'b0),
    .out(B[3]), .sel({x, y, z}));
  Multiplexer #(.select(3), .enable("false")) multiplexer_8 (
    .in0(1'b0), .in1(1'b1), .in2(1'b1), .in3(not_1_out), .in4(1'b1), .in5(1'b0), .in6(1'b0), .in7(1'b0),
    .out(B[2]), .sel({x, y, z}));
  Multiplexer #(.select(3), .enable("false")) multiplexer_9 (
    .in0(1'b0), .in1(1'b0), .in2(1'b0), .in3(1'b0), .in4(1'b0), .in5(1'b0), .in6(1'b0), .in7(1'b0),
    .out(B[1]), .sel({x, y, z}));
  Multiplexer #(.select(3), .enable("false")) multiplexer_10 (
    .in0(not_1_out), .in1(1'b1), .in2(w), .in3(not_1_out), .in4(1'b1), .in5(1'b0), .in6(1'b0), .in7(1'b0),
    .out(B[0]), .sel({x, y, z}));
  Multiplexer #(.select(3), .enable("false")) multiplexer_11 (
    .in0(1'b1), .in1(1'b1), .in2(1'b1), .in3(1'b1), .in4(1'b1), .in5(1'b0), .in6(1'b0), .in7(1'b0),
    .out(C[4]), .sel({x, y, z}));
  Multiplexer #(.select(3), .enable("false")) multiplexer_12 (
    .in0(1'b1), .in1(1'b1), .in2(not_1_out), .in3(w), .in4(1'b1), .in5(1'b0), .in6(1'b0), .in7(1'b0),
    .out(C[3]), .sel({x, y, z}));
  Multiplexer #(.select(3), .enable("false")) multiplexer_13 (
    .in0(1'b1), .in1(1'b1), .in2(1'b1), .in3(1'b1), .in4(1'b1), .in5(1'b0), .in6(1'b0), .in7(1'b0),
    .out(C[2]), .sel({x, y, z}));
  Multiplexer #(.select(3), .enable("false")) multiplexer_14 (
    .in0(1'b1), .in1(w), .in2(1'b1), .in3(1'b1), .in4(1'b1), .in5(1'b0), .in6(1'b0), .in7(1'b0), .out(C[1]),
    .sel({x, y, z}));
  Multiplexer #(.select(3), .enable("false")) multiplexer_15 (
    .in0(1'b1), .in1(1'b1), .in2(1'b1), .in3(1'b1), .in4(1'b1), .in5(1'b0), .in6(1'b0), .in7(1'b0),
    .out(C[0]), .sel({x, y, z}));
endmodule

module _5_bit_register (
  input  Enable,
  input  Clock,
  input  Clear,
  input  [4:0] D,
  output [4:0] Q
);

  wire and_1_out;

  and and_1 (and_1_out, Enable, Clock);
  D_Flip_Flop d_ff_1 (.clk(and_1_out), .D(D[4]), .Q(Q[4]), .reset(Clear));  // open: Qn, preset, en
  D_Flip_Flop d_ff_2 (.clk(and_1_out), .D(D[3]), .Q(Q[3]), .reset(Clear));  // open: Qn, preset, en
  D_Flip_Flop d_ff_3 (.clk(and_1_out), .D(D[2]), .Q(Q[2]), .reset(Clear));  // open: Qn, preset, en
  D_Flip_Flop d_ff_4 (.clk(and_1_out), .D(D[1]), .Q(Q[1]), .reset(Clear));  // open: Qn, preset, en
  D_Flip_Flop d_ff_5 (.clk(and_1_out), .D(D[0]), .Q(Q[0]), .reset(Clear));  // open: Qn, preset, en
endmodule

module multi_bit_shift_register (
  input  Clock,
  input  Enable,
  input  Clear,
  input  [4:0] _5_bit_input,
  output [4:0] Q1__5_bit_output,
  output [4:0] Q2__5_bit_output,
  output [4:0] Q3__5_bit_output,
  output [4:0] Q4__5_bit_output,
  output [4:0] Q5__5_bit_output
);

  _5_bit_register u_5_bit_register_1 (
    .Enable(Enable), .Clock(Clock), .D(_5_bit_input), .Q(Q1__5_bit_output), .Clear(Clear));
  _5_bit_register u_5_bit_register_2 (
    .Enable(Enable), .Clock(Clock), .D(Q1__5_bit_output), .Q(Q2__5_bit_output), .Clear(Clear));
  _5_bit_register u_5_bit_register_3 (
    .Enable(Enable), .Clock(Clock), .D(Q2__5_bit_output), .Q(Q3__5_bit_output), .Clear(Clear));
  _5_bit_register u_5_bit_register_4 (
    .Enable(Enable), .Clock(Clock), .D(Q3__5_bit_output), .Q(Q4__5_bit_output), .Clear(Clear));
  _5_bit_register u_5_bit_register_5 (
    .Enable(Enable), .Clock(Clock), .D(Q4__5_bit_output), .Q(Q5__5_bit_output), .Clear(Clear));
endmodule
