// Logisim project project_extra.circ as structural Verilog: 2 circuits, main circuit main
module main (
);

  wire _0_out, _1_out, _2_out, _2hz_out, _3_out, _4_out, _4hz_out, _5_out, _6_out, _7_out, _8_out, _8hz_out,
       _9_out, _10_out, _11_out, _12_out, _13_out, _14_out, _15_out, and_1_out, clock_1_out, d_ff_1_q,
       d_ff_1_qn, multiplexer_1_out, not_1_out, OFF_out, or_1_out, priority_encoder_1_gs,
       priority_encoder_2_en_out, priority_encoder_2_gs;
  wire [1:0] priority_encoder_1_out, register_1_q;
  wire [2:0] counter_1_q, counter_2_q;
  wire [3:0] priority_encoder_2_out, register_2_q;
  wire [4:0] display_func_1_a, display_func_1_b, display_func_1_c, display_func_1_e, multiplexer_2_out,
       shift_register_1_q0, shift_register_1_q1, shift_register_1_q2, shift_register_1_q3,
       shift_register_1_q4;

  Button _8hz (.out(_8hz_out));
  Button _4hz (.out(_4hz_out));
  Button _2hz (.out(_2hz_out));
  Button _10 (.out(_10_out));
  Button _11 (.out(_11_out));
  Button _12 (.out(_12_out));
  Button _15 (.out(_15_out));
  Button _14 (.out(_14_out));
  Button _13 (.out(_13_out));
  Button _1 (.out(_1_out));
  Button _3 (.out(_3_out));
  Button _2 (.out(_2_out));
  Button _6 (.out(_6_out));
  Button _4 (.out(_4_out));
  Button _5 (.out(_5_out));
  Button _9 (.out(_9_out));
  Button _7 (.out(_7_out));
  Button _8 (.out(_8_out));
  Button _0 (.out(_0_out));
  Button OFF (.out(OFF_out));
  DotMatrix #(.matrixrows(5)) dotmatrix_1 (
    .col0(shift_register_1_q0), .col1(shift_register_1_q1), .col2(shift_register_1_q2),
    .col3(shift_register_1_q3), .col4(shift_register_1_q4));
  Priority_Encoder #(.select(2)) priority_encoder_1 (
    .in0(OFF_out), .in1(_8hz_out), .in2(_4hz_out), .in3(_2hz_out), .out(priority_encoder_1_out),
    .gs(priority_encoder_1_gs));  // open: en_out, en_in
  not not_1 (not_1_out, priority_encoder_2_en_out);
  or or_1 (or_1_out, OFF_out, not_1_out);
  Register #(.width(2), .trigger("high")) register_1 (
    .D(priority_encoder_1_out), .en(priority_encoder_1_gs), .Q(register_1_q), .clk(1'b1));  // open: clr
  Priority_Encoder #(.select(4)) priority_encoder_2 (
    .in0(_0_out), .in1(_1_out), .in2(_2_out), .in3(_3_out), .in4(_4_out), .in5(_5_out), .in6(_6_out),
    .in7(_7_out), .in8(_8_out), .in9(_9_out), .in10(_10_out), .in11(_11_out), .in12(_12_out), .in13(_13_out),
    .in14(_14_out), .in15(_15_out), .out(priority_encoder_2_out), .gs(priority_encoder_2_gs),
    .en_out(priority_encoder_2_en_out));  // open: en_in
  D_Flip_Flop #(.trigger("high")) d_ff_1 (
    .Q(d_ff_1_q), .Qn(d_ff_1_qn), .preset(not_1_out), .reset(OFF_out));  // open: clk, D, en
  Clock clock_1 (.out(clock_1_out));
  Register #(.width(4), .trigger("high")) register_2 (
    .D(priority_encoder_2_out), .en(priority_encoder_2_gs), .Q(register_2_q), .clk(d_ff_1_q), .clr(d_ff_1_qn));
  Counter #(.width(3), .max('h7)) counter_1 (.Q(counter_1_q), .clk(clock_1_out));  // open: load, D, count, carry, clr
  display_func display_func_1 (
    .x(register_2_q[3]), .E(display_func_1_e), .A(display_func_1_a), .B(display_func_1_b),
    .C(display_func_1_c), .y(register_2_q[2]), .w(register_2_q[0]), .z(register_2_q[1]));
  Multiplexer #(.select(2), .enable("false")) multiplexer_1 (
    .in0(1'b0), .in1(counter_1_q[0]), .in2(counter_1_q[1]), .in3(counter_1_q[2]), .out(multiplexer_1_out),
    .sel(register_1_q));
  DotMatrix #(.matrixrows(5)) dotmatrix_2 (
    .col0(display_func_1_e), .col1({5{1'b0}}), .col2(display_func_1_a), .col3(display_func_1_b),
    .col4(display_func_1_c));
  Multiplexer #(.select(3), .width(5), .enable("false")) multiplexer_2 (
    .in0(display_func_1_c), .in1(display_func_1_b), .in2(display_func_1_a), .in3({5{1'b0}}),
    .in4(display_func_1_e), .in5({5{1'b0}}), .in6({5{1'b0}}), .in7({5{1'b0}}), .out(multiplexer_2_out),
    .sel(counter_2_q));
  and and_1 (and_1_out, d_ff_1_q, multiplexer_1_out);
  Shift_Register #(.width(5), .length(5)) shift_register_1 (
    .shift(d_ff_1_q), .in(multiplexer_2_out), .clk(multiplexer_1_out), .clr(or_1_out),
    .q0(shift_register_1_q0), .q1(shift_register_1_q1), .q2(shift_register_1_q2), .q3(shift_register_1_q3),
    .q4(shift_register_1_q4));  // open: out, load, d0, d1, d2, d3, d4
  Counter #(.width(3), .max('h7)) counter_2 (
    .Q(counter_2_q), .clk(and_1_out), .clr(or_1_out));  // open: load, D, count, carry
endmodule

module display_func (
  input  x,
  input  z,
  input  w,
  input  y,
  output [4:0] E,
  output [4:0] A,
  output [4:0] B,
  output [4:0] C
);

  wire not_1_out;

  Multiplexer #(.select(3), .enable("false")) multiplexer_1 (
    .in0(1'b0), .in1(1'b0), .in2(1'b0), .in3(1'b0), .in4(1'b0), .in5(1'b1), .in6(1'b1), .in7(1'b1),
    .out(E[4]), .sel({x, y, z}));
  not not_1 (not_1_out, w);
  Multiplexer #(.select(3), .enable("false")) multiplexer_2 (
    .in0(not_1_out), .in1(1'b1), .in2(1'b1), .in3(1'b1), .in4(1'b1), .in5(not_1_out), .in6(1'b1), .in7(1'b1),
    .out(A[4]), .sel({x, y, z}));
  Multiplexer #(.select(3), .enable("false")) multiplexer_3 (
    .in0(not_1_out), .in1(1'b0), .in2(1'b1), .in3(not_1_out), .in4(1'b1), .in5(not_1_out), .in6(1'b0),
    .in7(1'b1), .out(A[3]), .sel({x, y, z}));
  Multiplexer #(.select(3), .enable("false")) multiplexer_4 (
    .in0(not_1_out), .in1(1'b1), .in2(1'b1), .in3(not_1_out), .in4(1'b1), .in5(not_1_out), .in6(1'b1),
    .in7(1'b1), .out(A[2]), .sel({x, y, z}));
  Multiplexer #(.select(3), .enable("false")) multiplexer_5 (
    .in0(not_1_out), .in1(not_1_out), .in2(1'b0), .in3(not_1_out), .in4(not_1_out), .in5(not_1_out),
    .in6(not_1_out), .in7(1'b0), .out(A[1]), .sel({x, y, z}));
  Multiplexer #(.select(3), .enable("false")) multiplexer_6 (
    .in0(not_1_out), .in1(1'b1), .in2(w), .in3(not_1_out), .in4(1'b1), .in5(not_1_out), .in6(1'b1), .in7(w),
    .out(A[0]), .sel({x, y, z}));
  Multiplexer #(.select(3), .enable("false")) multiplexer_7 (
    .in0(not_1_out), .in1(1'b1), .in2(w), .in3(1'b1), .in4(1'b1), .in5(not_1_out), .in6(1'b1), .in7(w),
    .out(B[4]), .sel({x, y, z}));
  Multiplexer #(.select(3), .enable("false")) multiplexer_8 (
    .in0(1'b0), .in1(1'b0), .in2(1'b0), .in3(1'b0), .in4(1'b0), .in5(1'b0), .in6(1'b0), .in7(1'b0),
    .out(B[3]), .sel({x, y, z}));
  Multiplexer #(.select(3), .enable("false")) multiplexer_9 (
    .in0(1'b0), .in1(1'b1), .in2(1'b1), .in3(not_1_out), .in4(1'b1), .in5(1'b0), .in6(1'b1), .in7(1'b1),
    .out(B[2]), .sel({x, y, z}));
  Multiplexer #(.select(3), .enable("false")) multiplexer_10 (
    .in0(1'b0), .in1(1'b0), .in2(1'b0), .in3(1'b0), .in4(1'b0), .in5(1'b0), .in6(1'b0), .in7(1'b0),
    .out(B[1]), .sel({x, y, z}));
  Multiplexer #(.select(3), .enable("false")) multiplexer_11 (
    .in0(not_1_out), .in1(1'b1), .in2(w), .in3(not_1_out), .in4(1'b1), .in5(not_1_out), .in6(1'b1), .in7(w),
    .out(B[0]), .sel({x, y, z}));
  Multiplexer #(.select(3), .enable("false")) multiplexer_12 (
    .in0(1'b1), .in1(1'b1), .in2(1'b1), .in3(1'b1), .in4(1'b1), .in5(1'b1), .in6(1'b1), .in7(1'b1),
    .out(C[4]), .sel({x, y, z}));
  Multiplexer #(.select(3), .enable("false")) multiplexer_13 (
    .in0(1'b1), .in1(1'b1), .in2(not_1_out), .in3(w), .in4(1'b1), .in5(1'b1), .in6(1'b1), .in7(not_1_out),
    .out(C[3]), .sel({x, y, z}));
  Multiplexer #(.select(3), .enable("false")) multiplexer_14 (
    .in0(1'b1), .in1(1'b1), .in2(1'b1), .in3(1'b1), .in4(1'b1), .in5(1'b1), .in6(1'b1), .in7(1'b1),
    .out(C[2]), .sel({x, y, z}));
  Multiplexer #(.select(3), .enable("false")) multiplexer_15 (
    .in0(1'b1), .in1(w), .in2(1'b1), .in3(1'b1), .in4(1'b1), .in5(1'b1), .in6(w), .in7(1'b1), .out(C[1]),
    .sel({x, y, z}));
  Multiplexer #(.select(3), .enable("false")) multiplexer_16 (
    .in0(1'b1), .in1(1'b1), .in2(1'b1), .in3(1'b1), .in4(1'b1), .in5(1'b1), .in6(1'b1), .in7(1'b1),
    .out(C[0]), .sel({x, y, z}));

  assign E[3:0] = {4{E[4]}};
endmodule
